# Fritzing sketch Sign to Text Converter (saved by Fritzing 0.9.3b)
breadboards: 1

parts:
  R1 = Basic Flex Resistor
  R2 = Basic Flex Resistor
  R3 = Basic Flex Resistor
  R4 = Basic Flex Resistor
  R5 = Basic Flex Resistor
  Part1 = Arduino Nano (Rev3.0)
  Part2 = Triple Axis Accelerometer Breakout - ADXL335

nets:
  N1: R1.Pin_2, Part1.A4
  5V: R1.pin_1, R2.pin_1, R3.pin_1, R4.pin_1, R5.pin_1, Part1.5V, Part2.VCC
  N2: R2.Pin_2, Part1.A3
  N3: R3.Pin_2, Part1.A2
  N4: R4.Pin_2, Part1.A0
  N5: R5.Pin_2, Part1.A1
  N6: Part1.A7, Part2.ZOUT
  N7: Part1.A6, Part2.YOUT
  N8: Part1.A5, Part2.XOUT
